# Fritzing sketch poulailler (saved by Fritzing 0.9.2b)

parts:
  MOTOR1 = 28BYJ-48 Stepper Motor
  BREAKOUT1 = ULN2003A breakout board
  ZS-042_RTC1 = ZS-042 RTC Module
  Composant1 = Arduino Nano (Rev3.0)
  S1 = Round Pushbutton

nets:
  N1: MOTOR1.RED, BREAKOUT1.RED_wire
  N2: MOTOR1.ORANGE, BREAKOUT1.ORANGE_wire
  N3: MOTOR1.YELLOW, BREAKOUT1.YELLOW_wire
  N4: MOTOR1.PINK, BREAKOUT1.PINK_wire
  N5: MOTOR1.BLUE, BREAKOUT1.BLUE_wire
  N6: BREAKOUT1.In_1, Composant1.D7
  N7: BREAKOUT1.In_2, Composant1.D6
  N8: BREAKOUT1.In_3, Composant1.D5
  N9: BREAKOUT1.In_4, Composant1.D4
  GND: BREAKOUT1.0V, ZS-042_RTC1.GND, Composant1.GND, S1.leg1
  +5V: BREAKOUT1.+5V, ZS-042_RTC1.VCC, Composant1.5V
  N10: ZS-042_RTC1.SDA, Composant1.A4
  N11: ZS-042_RTC1.SCL, Composant1.A5
  N12: ZS-042_RTC1.SQW, Composant1.D2
  N13: Composant1.D3, S1.leg0

custom parts:
  ULN2003A breakout board: ULN2003A 7-way Darlington Transistor Driver on breakoutboard
